# Fritzing sketch Diagrama Robot (saved by Fritzing 0.9.2b)
breadboards: 4

parts:
  Raspberry_Pi1 = Raspberry Pi 2
  Part3 = SRF05 Ultrasonic Rangefinder
  Part4 = SRF05 Ultrasonic Rangefinder
  Part5 = SRF05 Ultrasonic Rangefinder
  R1 = Resistor [tolerance=±5% resistance=1k package="2010 [SMD]"]
  IC1 = L293D [package=THT]
  VCC1 = 4 x AAA Battery Mount
  R2 = Resistor [tolerance=±5% resistance=1k package="2010 [SMD]"]
  R3 = Resistor [tolerance=±5% resistance=1k package="2010 [SMD]"]
  R4 = Resistor [tolerance=±5% resistance=12k package="2010 [SMD]"]
  R5 = Resistor [tolerance=±5% resistance=12k package="2010 [SMD]"]
  R6 = Resistor [tolerance=±5% resistance=12k package="2010 [SMD]"]
  M1 = DC Motor
  M2 = DC Motor

nets:
  N1: Raspberry_Pi1.GPIO4, R3.Pin_1, R6.Pin_1
  N2: Raspberry_Pi1.GPIO17, Part3.Trig
  N3: Raspberry_Pi1.GPIO22, Part4.Trig
  N4: Raspberry_Pi1.GPIO5, IC1.In_3
  N5: Raspberry_Pi1.GPIO6, IC1.In_4
  N6: Raspberry_Pi1.GPIO13, IC1.In_2
  N7: Raspberry_Pi1.GPIO19, IC1.In_1
  N8: Raspberry_Pi1.GND, R1.Pin_1, R4.Pin_1
  VCC: Part3.VCC, Part4.VCC, Part5.VCC, IC1.+V
  N9: Part3.Echo, R3.Pin_0
  GND: Part3.GND, Part4.GND, Part5.GND, IC1.0V, VCC1.-, R4.Pin_0, R5.Pin_0, R6.Pin_0
  N10: Part4.Echo, R2.Pin_0
  N11: Part5.Echo, R1.Pin_0
  N12: IC1.Out_1_(_Controlled_by_Enable_1_), M2.pin_2
  N13: IC1.Out_2_(_Controlled_by_Enable_1_), M2.pin_1
  N14: IC1.+Vmotor, VCC1.+
  N15: IC1.Out_3_(_Controlled_by_Enable_2_), M1.pin_2
  N16: IC1.Out_4_(_Controlled_by_Enable_2_), M1.pin_1
  N17: R2.Pin_1, R5.Pin_1
